# Fritzing sketch Parking_Sensor_fritizing (saved by Fritzing 0.9.2b)
breadboards: 1

parts:
  LCD1 = LCD screen
  Componente1 = Sonar Ultrasonic Rangefinder
  Componente2 = Arduino Uno (Rev3)
  J1 = Piezo Speaker
  LED1 = LED - 5mm [color="Red (633nm)" package="5 mm [THT]"]  # not connected
  U2 = POT [package=pot_alpha_rv16af-20]
  R1 = Resistor [tolerance=±5% resistance=220 package=THT]

nets:
  GND: LCD1.VSS, LCD1.R/W, LCD1.LED-, Componente1.GND, Componente2.GND, J1.pin1, U2.E
  VDD: LCD1.VDD, Componente1.Sonar_Ultrasonic_Rangefinder, Componente2.5V, U2.A, R1.Pin_0
  N1: LCD1.V0, U2.S
  N2: LCD1.RS, Componente2.D12/MISO
  N3: LCD1.E, Componente2.D11_PWM/MOSI
  N4: LCD1.DB4, Componente2.D5_PWM
  N5: LCD1.DB5, Componente2.D4
  N6: LCD1.DB6, Componente2.D3_PWM
  N7: LCD1.DB7, Componente2.D2
  N8: LCD1.LED+, R1.Pin_1
  N9: Componente1.Trig, Componente2.D8
  N10: Componente1.Echo, Componente2.D7
  N11: Componente2.D10_PWM/SS, J1.pin2
